# Fritzing sketch tavanyar-arduino (saved by Fritzing 0.9.3b)
breadboards: 1

parts:
  Arduino_Uno = Arduino Uno (Rev3)
  HC-05 = Bluetooth HC-05 Macho
  MPU-6050_1 = InvenSense MPU6050
  MPU-6050_2 = InvenSense MPU6050
  Resistor_1 = Resistor [tolerance=±5% resistance=1k package="0402 [SMD]"]
  Resistor_2 = Resistor [tolerance=±5% resistance=1k package="0402 [SMD]"]
  Resistor_3 = Resistor [tolerance=±5% resistance=1k package="0402 [SMD]"]

nets:
  N1: Arduino_Uno.A4/SDA, MPU-6050_1.SDA, MPU-6050_2.SDA
  N2: Arduino_Uno.A5/SCL, MPU-6050_1.SCL, MPU-6050_2.SCL
  N3: Arduino_Uno.D12/MISO, MPU-6050_2.AD0
  N4: Arduino_Uno.D13/SCK, MPU-6050_1.AD0
  N5: Arduino_Uno.D2, HC-05.TXD
  N6: Arduino_Uno.D3_PWM, Resistor_1.Pin_0
  VCC: Arduino_Uno.5V, HC-05.VCC, MPU-6050_1.VCC, MPU-6050_2.VCC
  GND: Arduino_Uno.GND, HC-05.GND, MPU-6050_1.GND, MPU-6050_2.GND, Resistor_3.Pin_1
  N7: HC-05.RXD, Resistor_1.Pin_1, Resistor_2.Pin_0
  N8: Resistor_2.Pin_1, Resistor_3.Pin_0
